# Fritzing sketch gml_fieldrecorder (saved by Fritzing 0.6.2b)
breadboards: 1

parts:
  U1 = mystery part, 4 pins [chip_label=9DOF spacing=300mil]
  C1 = Ceramic Capacitor [capacitance=100nF package="100 mil [THT, multilayer]"]
  C2 = Ceramic Capacitor [capacitance=100nF package="100 mil [THT, multilayer]"]
  C4 = Tantalum Capacitor [capacitance="1 μF" package="100 mil [THT, tantalum]"]
  U3 = Voltage Regulator - 3.3V [package="TO220 [THT]"]
  C3 = Tantalum Capacitor [capacitance="1 μF" package="100 mil [THT, tantalum]"]
  U4 = mystery part, 7 pins [chip_label="SD CARD" spacing=300mil]
  LED1 = Red LED - 5mm [package="5 mm [THT]"]
  LED2 = Red LED - 5mm [package="5 mm [THT]"]
  IC1 = IC, DIP package, 8 pins [chip_label=Prox spacing=300mil]
  S1 = Pushbutton [package=THT]
  R1 = Resistor [tolerance=±5% resistance=220 package=THT]
  C5 = Ceramic Capacitor [capacitance=2.2µF package="100 mil [THT, multilayer]"]
  C6 = Ceramic Capacitor [capacitance=2.2µF package="100 mil [THT, multilayer]"]
  U5 = mystery part, 2 pins [chip_label=Foil spacing=300mil]
  U6 = Mystery_Part___8_pins
  Teensy++1 = Teensy++ 2.0

nets:
  N1: U1.pin1, U3.output_voltage, U4.pin5
  N2: U1.pin2, Teensy++1.B1
  N3: U1.pin3, Teensy++1.B0
  GND: U1.pin4, C1.0, C2.1, C4.-, U3.GND, C3.+, U4.pin3, LED1.cathode, LED2.cathode, IC1.pin2, IC1.pin4, R1.Pin_1, C5.0, C6.0, U5.pin2, U6.connector5, Teensy++1.GND
  N4: C1.1, C3.-, U6.connector6
  N5: C2.0, C4.+, U3.input_voltage, IC1.pin5, S1.leg0, C5.1, U6.connector4, Teensy++1.VCC
  N6: U4.pin2, Teensy++1.C3
  N7: U4.pin4, Teensy++1.C2
  N8: U4.pin6, Teensy++1.C1
  N9: U4.pin7, Teensy++1.C0
  N10: LED1.anode, Teensy++1.E7
  N11: LED2.anode, Teensy++1.E6
  N12: IC1.pin1, U5.pin1
  N13: IC1.pin3, C6.1
  N14: IC1.pin6, Teensy++1.F0
  N15: S1.leg1, R1.Pin_0, Teensy++1.E4
  N16: U6.connector0, Teensy++1.B3
  N17: U6.connector3, Teensy++1.B4
  N18: U6.connector7, Teensy++1.B2
